# Fritzing sketch lcd (saved by Fritzing 0.9.3b)
breadboards: 1

parts:
  IC1 = PIC16F628 [package="DIP (Dual Inline) [THT]"]
  R1 = Rotary Potentiometer (Small) [maximum_resistance=1kΩ package=THT]
  LCD1 = LCD screen

nets:
  N1: IC1.pin5, R1.leg2, LCD1.VSS
  N2: IC1.pin6, LCD1.DB4
  N3: IC1.pin7, LCD1.DB5
  N4: IC1.pin8, LCD1.DB6
  N5: IC1.pin9, LCD1.DB7
  N6: IC1.pin10, LCD1.RS
  N7: IC1.pin11, LCD1.E
  N8: IC1.pin12, LCD1.R/W
  N9: IC1.pin14, R1.leg1, LCD1.VDD
  N10: R1.wiper, LCD1.V0

custom parts:
  PIC16F628: PIC16F628 - A FLASH-Based 8-Bit CMOS Microcontroller. 18pin-PDIP.
