# Fritzing sketch serial-communication-transmission (saved by Fritzing 0.9.3b)
breadboards: 1

parts:
  IC1 = PIC16F628 [package="DIP (Dual Inline) [THT]"]
  パーツ1 = Arduino Uno (Rev3)

nets:
  N1: IC1.pin5, パーツ1.GND
  N2: IC1.pin8, パーツ1.D0/RX
  N3: IC1.pin14, パーツ1.5V

custom parts:
  PIC16F628: PIC16F628 - A FLASH-Based 8-Bit CMOS Microcontroller. 18pin-PDIP.
