# Fritzing sketch seven-segment-led-counter (saved by Fritzing 0.9.3b)
breadboards: 2

parts:
  OSL10561-IB = 7-Segment LED Display [package=THT]
  OSL10561-IB_2 = 7-Segment LED Display [package=THT]
  R1 = Resistor [tolerance=±5% resistance=100 package=THT]
  R2 = Resistor [tolerance=±5% resistance=100 package=THT]
  IC1 = PIC16F628 [package="DIP (Dual Inline) [THT]"]

nets:
  N1: OSL10561-IB.cathodeE, OSL10561-IB_2.cathodeE, IC1.pin13
  N2: OSL10561-IB.cathodeD, OSL10561-IB_2.cathodeD, IC1.pin12
  N3: OSL10561-IB.commAnode#2, R1.Pin_1
  N4: OSL10561-IB.cathodeC, OSL10561-IB_2.cathodeC, IC1.pin11
  N5: OSL10561-IB.cathodeB, OSL10561-IB_2.cathodeB, IC1.pin10
  N6: OSL10561-IB.cathodeA, OSL10561-IB_2.cathodeA, IC1.pin9
  N7: OSL10561-IB.cathodeF, OSL10561-IB_2.cathodeF, IC1.pin8
  N8: OSL10561-IB.cathodeG, OSL10561-IB_2.cathodeG, IC1.pin7
  N9: OSL10561-IB_2.commAnode#2, R2.Pin_1
  N10: R1.Pin_0, IC1.pin17
  N11: R2.Pin_0, IC1.pin18

custom parts:
  PIC16F628: PIC16F628 - A FLASH-Based 8-Bit CMOS Microcontroller. 18pin-PDIP.
