# Fritzing sketch xbee-serial-communication-transmission (saved by Fritzing 0.9.3b)
breadboards: 1

parts:
  U1 = XBee
  IC1 = PIC16F628 [package="DIP (Dual Inline) [THT]"]

nets:
  N1: U1.VCC, IC1.pin14
  N2: U1.pin3, IC1.pin8
  N3: U1.GND, IC1.pin5

custom parts:
  PIC16F628: PIC16F628 - A FLASH-Based 8-Bit CMOS Microcontroller. 18pin-PDIP.
